# Fritzing sketch BT_PAF_Nantes (saved by Fritzing 0.9.2b)

parts:
  부품1 = Arduino Uno (Rev3)
  부품2 = Bluetooth HC-06

nets:
  N1: 부품1.D10_PWM/SS, 부품2.TXD
  N2: 부품1.D11_PWM/MOSI, 부품2.RXD
  5V: 부품1.5V, 부품2.VCC
  GND: 부품1.GND, 부품2.GND
