# Fritzing sketch BT_piloter_DEL (saved by Fritzing 0.9.3b)

parts:
  부품1 = Arduino Uno (Rev3)
  부품2 = Bluetooth HC-06
  LED1 = LED - 5mm [color="Red (633nm)" package="5 mm [THT]"]

nets:
  N1: 부품1.D8, LED1.anode
  N2: 부품1.D10_PWM/SS, 부품2.TXD
  N3: 부품1.D11_PWM/MOSI, 부품2.RXD
  5V: 부품1.5V, 부품2.VCC
  GND: 부품1.GND, 부품2.GND, LED1.cathode
