# Fritzing sketch HC-SR04 (saved by Fritzing 0.9.3b)
breadboards: 1

parts:
  Composant1 = Arduino Uno (Rev3)
  LED1 = LED - 5mm [color="Red (633nm)" package="5 mm [THT]"]
  R1 = Resistor [tolerance=±5% resistance=220 package=THT]
  hc-sr1 = hc-sr04

nets:
  N1: Composant1.D8, LED1.anode
  N2: Composant1.D5_PWM, hc-sr1.Echo
  N3: Composant1.D6_PWM, hc-sr1.Trig
  5V: Composant1.5V, hc-sr1.VCC
  GND: Composant1.GND, R1.Pin_0, hc-sr1.GND
  N4: LED1.cathode, R1.Pin_1

notes:
  Capteur à ultrasons
  HC-SR04
