# Fritzing sketch RFID_test (saved by Fritzing 0.9.3b)
breadboards: 1

parts:
  Composant1 = Arduino Uno (Rev3)
  R1 = Resistor [tolerance=±5% resistance=1k package="2512 [SMD]"]
  R2 = Resistor [tolerance=±5% resistance=1k package="2512 [SMD]"]
  LED1 = smd LED [color="Red (633nm)" package="0805 [SMD]"]
  LED2 = smd LED [color="Green (570nm)" package="0805 [SMD]"]
  Composant2 = RFID-RC522-v2

nets:
  N1: Composant1.D9_PWM, Composant2.RST
  N2: Composant1.D10_PWM/SS, Composant2.SDA
  N3: Composant1.D11_PWM/MOSI, Composant2.MOSI
  N4: Composant1.D12/MISO, Composant2.MISO
  N5: Composant1.D13/SCK, Composant2.SCK
  GND: Composant1.GND, R1.Pin_1, R2.Pin_1, Composant2.GND
  N6: Composant1.D2, LED2.anode
  N7: Composant1.D3_PWM, LED1.anode
  3V3: Composant1.3V3, Composant2.3.3V
  N8: R1.Pin_0, LED1.cathode
  N9: R2.Pin_0, LED2.cathode

notes:
  Module RFID
  Contrôler l'accès à l'aide d'un tag

custom parts:
  RFID-RC522-v2: A simple China made RFID-RC522 Reader; do check the pin labels, as this is a MFRC522 based clone.
