# Fritzing sketch Starter_Kit_prj6 (saved by Fritzing 0.9.3b)
breadboards: 1

parts:
  Arduino1 = Arduino Uno (Rev3)
  R9 = Photocell (LDR) [package=THT]
  R11 = Resistor [tolerance=±5% resistance=10k package=THT]
  J1 = Piezo Speaker

nets:
  N1: Arduino1.A0, R9.pin_0, R11.Pin_1
  N2: Arduino1.D8, J1.pin2
  N3: Arduino1.5V, R9.pin_1
  N4: Arduino1.GND, R11.Pin_0, J1.pin1

notes:
  Starter Kit (projet 6)
  Thérémine lumineux
