# Fritzing sketch Starter_Kit_prj7 (saved by Fritzing 0.9.3b)
breadboards: 1

parts:
  Arduino1 = Arduino Uno (Rev3)
  R11 = Resistor [tolerance=±5% resistance=10k package=THT]
  J1 = Piezo Speaker
  S1 = Pushbutton [package="[THT]"]
  S2 = Pushbutton [package="[THT]"]
  S3 = Pushbutton [package="[THT]"]
  S4 = Pushbutton [package="[THT]"]
  R12 = Resistor [tolerance=±5% resistance=220 package=THT]
  R13 = Resistor [tolerance=±5% resistance=1M package=THT]
  R14 = Resistor [tolerance=±5% resistance=10k package=THT]

nets:
  N1: Arduino1.A0, S1.Pin_1, S1.Pin_2, S2.Pin_1, S2.Pin_2, S3.Pin_1, S3.Pin_2, S4.Pin_1, S4.Pin_2, R14.Pin_1
  N2: Arduino1.D8, J1.pin2
  N3: Arduino1.5V, R11.Pin_0, S1.Pin_3, S1.Pin_4, R12.Pin_0, R13.Pin_0
  N4: Arduino1.GND, J1.pin1, R14.Pin_0
  N5: R11.Pin_1, S3.Pin_3, S3.Pin_4
  N6: S2.Pin_3, S2.Pin_4, R13.Pin_1
  N7: S4.Pin_3, S4.Pin_4, R12.Pin_1

notes:
  Starter Kit (projet 7)
  Clavier musical
