# Fritzing sketch Starter_Kit_prj2 (saved by Fritzing 0.9.3b)
breadboards: 1

parts:
  Composant1 = Arduino Uno (Rev3)
  LED1 = LED - 5mm [color="Red (633nm)" package="5 mm [THT]"]
  LED2 = LED - 5mm [color="Red (633nm)" package="5 mm [THT]"]
  LED3 = LED - 5mm [color="Green (570nm)" package="5 mm [THT]"]
  S1 = Pushbutton [package="[THT]"]
  R1 = Resistor [tolerance=±5% resistance=220 package=THT]
  R2 = Resistor [tolerance=±5% resistance=220 package=THT]
  R3 = Resistor [tolerance=±5% resistance=220 package=THT]
  R4 = Resistor [tolerance=±5% resistance=10k package=THT]

nets:
  N1: Composant1.D2, S1.Pin_3, S1.Pin_4, R4.Pin_1
  N2: Composant1.D3_PWM, LED3.anode
  N3: Composant1.D4, LED2.anode
  N4: Composant1.D5_PWM, LED1.anode
  N5: Composant1.5V, S1.Pin_1, S1.Pin_2
  N6: Composant1.GND, R1.Pin_0, R2.Pin_0, R3.Pin_0, R4.Pin_0
  N7: LED1.cathode, R1.Pin_1
  N8: LED2.cathode, R2.Pin_1
  N9: LED3.cathode, R3.Pin_1

notes:
  Starter Kit (projet 2)
  Interface vaisseau spatial
