# Fritzing sketch Starter_Kit_prj5 (saved by Fritzing 0.9.3b)
breadboards: 1

parts:
  Arduino1 = Arduino Uno (Rev3)
  R1 = Rotary Potentiometer (Small) [maximum_resistance=100kΩ package=THT]
  J1 = Basic Servo
  C1 = Electrolytic Capacitor [capacitance=0.1mF voltage=20V package="100 mil [THT, electrolytic]"]
  C2 = Electrolytic Capacitor [capacitance=0.1mF voltage=20V package="100 mil [THT, electrolytic]"]

nets:
  N1: Arduino1.A0, R1.wiper
  N2: Arduino1.D9_PWM, J1.pulse
  5V: Arduino1.5V, R1.leg2, J1.vcc, C1.+, C2.+
  GND: Arduino1.GND, R1.leg1, J1.gnd, C1.-, C2.-

notes:
  Starter Kit (projet 5)
  Indicateur d'humeur
