# Fritzing sketch Starter_Kit_prj8 (saved by Fritzing 0.9.3b)
breadboards: 1

parts:
  Arduino1 = Arduino Uno (Rev3)
  R11 = Resistor [tolerance=±5% resistance=10k package=THT]
  R12 = Resistor [tolerance=±5% resistance=220 package=THT]
  R13 = Resistor [tolerance=±5% resistance=220 package=THT]
  R14 = Resistor [tolerance=±5% resistance=220 package=THT]
  LED1 = LED - 5mm [color="Red (633nm)" package="5 mm [THT]"]
  LED2 = LED - 5mm [color="Red (633nm)" package="5 mm [THT]"]
  LED3 = LED - 5mm [color="Red (633nm)" package="5 mm [THT]"]
  LED4 = LED - 5mm [color="Red (633nm)" package="5 mm [THT]"]
  LED5 = LED - 5mm [color="Red (633nm)" package="5 mm [THT]"]
  LED6 = LED - 5mm [color="Red (633nm)" package="5 mm [THT]"]
  R15 = Resistor [tolerance=±5% resistance=220 package=THT]
  R17 = Resistor [tolerance=±5% resistance=220 package=THT]
  S1 = Tilt Switch [package=THT]
  R16 = Resistor [tolerance=±5% resistance=220 package=THT]

nets:
  N1: Arduino1.D8, R11.Pin_1, S1.Pin_2
  N2: Arduino1.D2, LED6.anode
  N3: Arduino1.D3_PWM, LED5.anode
  N4: Arduino1.D4, LED4.anode
  N5: Arduino1.D5_PWM, LED3.anode
  N6: Arduino1.D6_PWM, LED2.anode
  N7: Arduino1.D7, LED1.anode
  N8: Arduino1.5V, S1.Pin_1
  N9: Arduino1.GND, R11.Pin_0, R12.Pin_0, R13.Pin_0, R14.Pin_0, R15.Pin_0, R17.Pin_0, R16.Pin_0
  N10: R12.Pin_1, LED1.cathode
  N11: R13.Pin_1, LED2.cathode
  N12: R14.Pin_1, LED3.cathode
  N13: LED4.cathode, R15.Pin_1
  N14: LED5.cathode, R16.Pin_1
  N15: LED6.cathode, R17.Pin_1

notes:
  Starter Kit (projet 8)
  Sablier numérique
