# Fritzing sketch grenouille (saved by Fritzing 0.9.3b)
breadboards: 1

parts:
  Composant1 = Arduino Uno (Rev3)
  J1 = Basic Servo
  J2 = Basic Servo
  hc-sr1 = hc-sr04

nets:
  N1: Composant1.D4, hc-sr1.Trig
  N2: Composant1.D5_PWM, hc-sr1.Echo
  N3: Composant1.D6_PWM, J2.pulse
  N4: Composant1.D7, J1.pulse
  VCC: Composant1.5V, J1.vcc, J2.vcc, hc-sr1.VCC
  GND: Composant1.GND, J1.gnd, J2.gnd, hc-sr1.GND
