# Fritzing sketch infrarouge_test (saved by Fritzing 0.9.3b)
breadboards: 1

parts:
  Composant1 = Arduino Uno (Rev3)
  R1 = Resistor [tolerance=±5% resistance=1k package="2512 [SMD]"]
  LED1 = smd LED [color="Red (633nm)" package="0805 [SMD]"]
  Part1 = KY-022 Infrared Receiver Module [package="Breakout board"]

nets:
  N1: Composant1.D13/SCK, LED1.anode
  N2: Composant1.D2, Part1.S
  5V: Composant1.5V, Part1.Vin
  N3: Composant1.GND, R1.Pin_1, Part1.-
  N4: R1.Pin_0, LED1.cathode

notes:
  Module infrarouge (réception)
  Contrôler la réception d'un code

custom parts:
  KY-022 Infrared Receiver Module: Arduino IR receiver module KY-022, reacts to 38kHz infrared light.
